# Fritzing sketch v3 (saved by Fritzing 0.9.3b)
circuit board: 10cm x 10cm

parts:
  PW1 = Power plug
  S1 = Toggle Switch [package=THT]
  5v+ = female pin header, 5 pins [form="♀ (female)"]
  LM7805 = Voltage Regulator - 5V [package="TO220 [THT]"]
  100μF = Electrolytic Capacitor [capacitance=100μF package="100 mil [THT, electrolytic]"]
  12v+ = female pin header, 5 pins [form="♀ (female)"]
  12v- = female pin header, 5 pins [form="♀ (female)"]
  5v- = female pin header, 5 pins [form="♀ (female)"]
  +1 = Rectifier Diode [part_number=1N4001 package="300 mil [THT]"]
  1K1 = Resistor [tolerance=±5% resistance=220 package=THT]
  1 = LED - 3mm [color="Red (633nm)" package="3 mm [THT]"]
  LDR1 = Capacitor [package=cap-pth-small-kit]
  100k1 = Resistor [tolerance=±5% resistance=220 package=THT]
  0_1u1 = Ceramic Capacitor [capacitance=100nF package="100 mil [THT, multilayer]"]
  Atmega328P1 = atmega328 [package=dip]
  10K1 = Resistor [tolerance=±5% resistance=220 package=THT]
  XL1 = CRYSTAL - kHz [frequency="16 Mhz"]
  +5V_INV = Battery
  2 = LED - 3mm [color="Red (633nm)" package="3 mm [THT]"]
  22p1 = Capacitor [package=cap-pth-small-kit]
  22p2 = Capacitor [package=cap-pth-small-kit]
  -_+1 = Rectifier Diode [part_number=1N4001 package="300 mil [THT]"]
  RGB1 = RGB LED - (4 legs) [package="5 mm [THT]"]
  1K2 = Resistor [tolerance=±5% resistance=220 package=THT]
  R1 = Resistor [tolerance=±5% resistance=1k package=THT]
  DHT22 = female pin header, 3 pins [form="♀ (female)"]
  Moisture = USB Connectors [package=usb-a-h]
  Bluetooth_HC05 = female pin header, 6 pins [form="♀ (female)"]
  SPK = female pin header, 2 pins [form="♀ (female)"]
  DFPlayer_Mini = female pin header, 8 pins [form="♀ (female)"]
  R2 = Resistor [tolerance=±5% resistance=1k package=THT]
  WaterLevel = USB Connectors [package=usb-a-h]
  KY-3 = Keyes Relay [package=THT]
  KY-4 = Keyes Relay [package=THT]

nets:
  GND: PW1.GND, LM7805.GND, 100μF.-, 12v-.pin1, 12v-.pin2, 12v-.pin3, 12v-.pin4, 12v-.pin5, 5v-.pin1, 5v-.pin2, 5v-.pin3, 5v-.pin4, 5v-.pin5, 1K1.Pin_0, LDR1.2, Atmega328P1.GND, +5V_INV.+, 2.cathode, 22p1.1, 22p2.1, 1K2.Pin_1, DHT22.pin3, Moisture.GND, Bluetooth_HC05.pin4, DFPlayer_Mini.pin7, WaterLevel.GND, KY-3.ground, KY-4.ground
  N1: PW1.VCC, S1.L1
  N2: S1.COM, LM7805.input_voltage, 12v+.pin1, 12v+.pin2, 12v+.pin3, 12v+.pin4, 12v+.pin5, KY-3.power, KY-4.power
  N3: 5v+.pin1, 5v+.pin2, 5v+.pin3, 5v+.pin4, 5v+.pin5, LM7805.output_voltage, 100μF.+, +5V_INV.-, -_+1.anode, DFPlayer_Mini.pin1
  N4: +1.cathode, 1.anode, 100k1.Pin_0, Atmega328P1.VCC, Atmega328P1.AVCC, Atmega328P1.AREF, 10K1.Pin_0, -_+1.cathode, DHT22.pin1, Moisture.VBUS, WaterLevel.VBUS
  N5: 1K1.Pin_1, 1.cathode
  N6: LDR1.1, 100k1.Pin_1
  N7: 0_1u1.0, Atmega328P1.RESET, 10K1.Pin_1
  N8: Atmega328P1.D2, DHT22.pin2
  N9: Atmega328P1.D3_(PWM), Bluetooth_HC05.pin5
  N10: Atmega328P1.D4, Bluetooth_HC05.pin6
  N11: Atmega328P1.XLAT1, XL1.pin_0, 22p1.2
  N12: Atmega328P1.XLAT2, XL1.pin_1, 22p2.2
  N13: Atmega328P1.D5_(PWM), RGB1.blue_cathode, Bluetooth_HC05.pin3
  N14: Atmega328P1.D6_(PWM), RGB1.green_cathode, Bluetooth_HC05.pin2
  N15: Atmega328P1.D7, RGB1.red_cathode
  N16: Atmega328P1.D8, KY-3.signal
  N17: Atmega328P1.D9_(PWM), KY-4.signal
  N18: Atmega328P1.D10_(PWM), DFPlayer_Mini.pin3
  N19: Atmega328P1.D11_(PWM), Atmega328P1.D12, R2.Pin_0
  N20: Atmega328P1.D13, R1.Pin_0
  N21: Atmega328P1.A0, Moisture.D+
  N22: Atmega328P1.A1, WaterLevel.D+
  N23: 2.anode, R1.Pin_1
  N24: RGB1.common_anode, 1K2.Pin_0
  N25: SPK.pin1, DFPlayer_Mini.pin8
  N26: SPK.pin2, DFPlayer_Mini.pin6
  N27: DFPlayer_Mini.pin2, R2.Pin_1

notes:
  +12Vcc
  instagram:monteverde_ambiental
  Monteverde LTDA
  SISPRA REV - FelipheGomez
  Create by FelipheGomez
  www.monteverdeltda.com
  Fb:monteverdeforestalyambiental
  -
  .
  ----- Ardu5 -----
  GND
  -1K-
  16Mhz
  GND +V TX RX DTR
  +5V GND TX RX
  SDA
  SCL
  RX TX
  +5Vcc
  5´ 6´ 7  8
  RST 0  1  2  3´ 4  +  -
  13 12 11´10´ 9´ 8
  USB-Serial
  Bluetooth HC06
  A5 A4 A3 A2 A1 A0
  7.6.5

custom parts:
  Keyes Relay: The Keyes 5V relay module is suitable for SCM development, home appliance control. It uses a 5V~12V TIL control signal which can control DC / AC signal.
