# Fritzing sketch v1 (saved by Fritzing 0.9.3b)
breadboards: 1

parts:
  U5 = Voltage Regulator - 5V [package="TO220 [THT]"]
  C8 = Electrolytic Capacitor [capacitance=1µF package="100 mil [THT, electrolytic]"]
  C9 = Electrolytic Capacitor [capacitance=1µF package="100 mil [THT, electrolytic]"]
  S2 = Toggle Switch [package=THT]
  Power_plug2 = Power plug
  J3 = Generic male header - 2 pins [package=THT]

nets:
  N1: U5.input_voltage, C9.+, S2.COM
  GND: U5.GND, C8.-, C9.-, Power_plug2.GND, J3.pin2
  N2: U5.output_voltage, C8.+, J3.pin1
  N3: S2.L2, Power_plug2.VCC
