# Fritzing sketch 000002 (saved by Fritzing 0.9.3b)
circuit board: 6.83702cm x 5.31663cm

parts:
  Componente1 = Arduino Uno (Rev3)
  Componente4 = Bluetooth HC-05 Macho
  Componente5 = FC-28 Soil Hygrometer Module
  Componente7 = FC-28 Soil Hygrometer Module - Probe
  Water_Level_Sensor1 = Water Level Sensor
  VALVE1 = Plastic Solenoid Valve
  J3 = Power Jack [package=power_jack_pth_lock]
  KY-1 = Keyes Relay [package=THT]
  KY-2 = Keyes Relay [package=THT]
  LED3 = LEDs [package=led10mm]
  Componente2 = DHT22 Module FG
  JP7 = Header 3 [package=screwterminal-3.5mm-3_lock.007s]
  Power_plug1 = Power plug
  Power_plug2 = Power plug
  Power_plug3 = Power plug
  Power_plug4 = Power plug

nets:
  N1: Componente1.A0, Componente5.AO
  N2: Componente1.A1, Water_Level_Sensor1.SIG
  N3: Componente1.D8, KY-1.signal
  N4: Componente1.D9_PWM, KY-2.signal
  GND: Componente1.GND, Componente4.GND, Componente5.GND, Water_Level_Sensor1.GND, J3.GND, KY-1.ground, KY-2.ground, Componente2.GND, JP7.1, Power_plug2.GND, Power_plug3.GND
  N5: Componente1.D2, Componente2.OUT, JP7.2
  N6: Componente1.D3_PWM, Componente4.VCC
  N7: Componente1.D4, Componente4.Key
  N8: Componente1.D5_PWM, Componente4.TXD
  N9: Componente1.D6_PWM, Componente4.RXD
  VCC: Componente1.5V, Componente5.VCC, Water_Level_Sensor1.VCC, KY-1.power, KY-2.power
  VIN: Componente1.VIN, J3.PWR, KY-1.C, KY-2.NC, KY-2.C, KY-2.NO, Power_plug2.VCC
  N10: Componente5.POS, Componente7.POS
  N11: Componente5.NEG, Componente7.NEG
  N12: VALVE1.no_name_yet#1, Power_plug1.VCC
  N13: VALVE1.no_name_yet#2, Power_plug1.GND
  N14: KY-1.NO, Power_plug3.VCC
  N15: LED3.C, Power_plug4.GND
  N16: LED3.A, Power_plug4.VCC
  N17: Componente2.VCC, JP7.3

custom parts:
  FC-28 Soil Hygrometer Module: The FC-28 is a soil hygrometer module that uses the Texas Instruments LM393 comparator chip to provide an analog measurement of soil humidity. The digital output is high when soil moisture is over a certain threshold, as determined by adjusting the potentiometer.
  FC-28 Soil Hygrometer Module - Probe: The FC-28 is a soil hygrometer module that uses the Texas Instruments LM393 comparator chip to provide an analog measurement of soil humidity.
  Water Level Sensor: A water level sensor. This sensor operates at 3V to 5V. The Sig (signal) pin outputs an analogue signal that is in proportion to the amount of water in contact with the sensor.
  Keyes Relay: The Keyes 5V relay module is suitable for SCM development, home appliance control. It uses a 5V~12V TIL control signal which can control DC / AC signal.
  DHT22 Module FG: DHT22 module

// code stored in the sketch: 1_0_0.ino
/* 
#########################################################
#    Processor:          Arduino UNO, MEGA ou Teensy++ 2.0
#    Language:           Wiring / C /Processing /Fritzing / Arduino IDE
#    Objectives:         Test Module - Tiny RTC DS1307 Z
#    Author:             Andres Felipe Gomez Maya
#    Date:               17/10/2019
#    place:              Medellin, Colombia
#########################################################
#  
#  RTC-I2C: DS:SCL->ARD:SCL  DS:SDA->ARD:SDA  DS:VCC->5V  DS:GND->GND
#           **NOTA**: se debe cargar dos veces este programa 1.Con la linea 9= RTC.adjust(DateTime(__DATE__, __TIME__));
#    
#    
#    
#    
*/

#include <Wire.h> 
#include "RTClib.h"
RTC_DS1307 RTC;
#define A0 A0

void setup () {
  Serial.begin(9600); // Establece la velocidad de datos del puerto serie
  Serial.println("Iniciando el puerto I2C");
  Wire.begin();  
  Serial.println("Abriendo Wire.");.

  if (! RTC.begin()) {
    Serial.println("RTC No Encontrado.");
    while (1);
  }

  if (! RTC.isrunning()) {
    Serial.println("RTC NO funciona!");
  }
  
  // RTC.adjust(DateTime(__DATE__, __TIME__)); // Establece la fecha y hora (Comentar una vez establecida la hora)
} 


void loop(){

  if (! RTC.isrunning()) {
    Serial.println("RTC NO funciona!");
  } else {
    DateTime now = RTC.now(); // Obtiene la fecha y hora del   RTC
    Serial.print(now.year(), DEC); // A§o
    Serial.print('/');
    Serial.print(now.month(), DEC); // Mes
    Serial.print('/');
    Serial.print(now.day(), DEC); // Dia
    Serial.print(' ');
    Serial.print(now.hour(), DEC); // Horas
    Serial.print(':');
    Serial.print(now.minute(), DEC); // Minutos
    Serial.print(':');
    Serial.print(now.second(), DEC); // Segundos
    Serial.println();
  }
}

// code stored in the sketch: test_ds1307z_0.ino
/* 
#########################################################
#    Processor:          Arduino UNO, MEGA ou Teensy++ 2.0
#    Language:           Wiring / C /Processing /Fritzing / Arduino IDE
#    Objectives:         Test Module - Tiny RTC DS1307 Z
#    Author:             Andres Felipe Gomez Maya
#    Date:               17/10/2019
#    place:              Medellin, Colombia
#########################################################
*/

//  Prueba de Reloj Tiempo Real (RTC) y Modulo I2C
//  Conexion:
//    Arduino UNO  SCL->SCL  SDA->SDA  VCC->5V  GND->GND
//  
//    NOTA: se debe cargar dos veces este programa 1.Con la linea 9= RTC.adjust(DateTime(__DATE__, __TIME__));

#include <Wire.h> 
#include "RTClib.h"
RTC_DS1307 RTC;

void setup () {
  Serial.begin(9600); // Establece la velocidad de datos del puerto serie
  Serial.println("Inicia el puerto I2C");
  
  Serial.println("Abriendo Wire.");
  Wire.begin(); // 
  
  Serial.println("RTC Begin.");
  RTC.begin(); // Inicia la comunicaci?n con el RTC
  // RTC.adjust(DateTime(__DATE__, __TIME__)); // Establece la fecha y hora (Comentar una vez establecida la hora)
}
void loop(){
  DateTime now = RTC.now(); // Obtiene la fecha y hora del RTC
  Serial.print(now.year(), DEC); // A?o
  Serial.print('/');
  Serial.print(now.month(), DEC); // Mes
  Serial.print('/');
  Serial.print(now.day(), DEC); // Dia
  Serial.print(' ');
  Serial.print(now.hour(), DEC); // Horas
  Serial.print(':');
  Serial.print(now.minute(), DEC); // Minutos
  Serial.print(':');
  Serial.print(now.second(), DEC); // Segundos
  Serial.println();
}
