# Fritzing sketch board (saved by Fritzing 0.9.3b)
breadboards: 1

parts:
  C1 = Electrolytic Capacitor [capacitance=10µF package="100 mil [THT, electrolytic]"]  # not connected
  C2 = Electrolytic Capacitor [capacitance=10µF package="100 mil [THT, electrolytic]"]  # not connected
  R1 = Resistor [tolerance=±5% resistance=220 package=THT]  # not connected
  LED-ON = LED - 5mm [color="Red (633nm)" package="5 mm [THT]"]  # not connected
  Power_plug1 = Power plug
  IC1 = Voltage Regulator [package=78xxl]  # not connected
  D1 = Rectifier Diode [part_number=1N4001 package="300 mil [THT]"]
  VIN1 = female pin header, 2 pins [form="♀ (female)"]
  J1 = Screw terminal - 2 pins [package=THT]
  X1 = USB Connectors [package=usb-a-h]
  J2 = female pin header, 2 pins [form="♀ (female)"]

nets:
  N1: Power_plug1.VCC, D1.anode, VIN1.pin1, J1.pin1, X1.VBUS
  GND: Power_plug1.GND, VIN1.pin2, J1.pin2, X1.GND, J2.pin2
  N2: D1.cathode, J2.pin1
