# Fritzing sketch SISPRA-MD-001-V-2-0-0 (saved by Fritzing 0.9.3b)
breadboards: 1

parts:
  Componente1 = Arduino Uno (Rev3)
  Tiny_RTC1 = Tiny RTC

nets:
  GND: Componente1.GND, Tiny_RTC1.GND
  N1: Componente1.A4/SDA, Tiny_RTC1.SDA
  N2: Componente1.A5/SCL, Tiny_RTC1.SCL
  5V: Componente1.5V, Tiny_RTC1.VCC

custom parts:
  Tiny RTC: Tiny RTC I2C module DS1370Z RTC and AT24C32 EEPROM

// code stored in the sketch: test_ds1307z_0.ino
/* 
#########################################################
#    Processor:          Arduino UNO, MEGA ou Teensy++ 2.0
#    Language:           Wiring / C /Processing /Fritzing / Arduino IDE
#    Objectives:         Test Module - Tiny RTC DS1307 Z
#    Author:             Andres Felipe Gomez Maya
#    Date:               17/10/2019
#    place:              Medellin, Colombia
#########################################################
*/

//  Prueba de Reloj Tiempo Real (RTC) y Modulo I2C
//  Conexion:
//    Arduino UNO  SCL->SCL  SDA->SDA  VCC->5V  GND->GND
//  
//    NOTA: se debe cargar dos veces este programa 1.Con la linea 9= RTC.adjust(DateTime(__DATE__, __TIME__));

#include <Wire.h> 
#include "RTClib.h"
RTC_DS1307 RTC;

void setup () {
  Serial.begin(9600); // Establece la velocidad de datos del puerto serie
  Serial.println("Inicia el puerto I2C");
  
  Serial.println("Abriendo Wire.");
  Wire.begin(); // 
  
  Serial.println("RTC Begin.");
  RTC.begin(); // Inicia la comunicaci¢n con el RTC
  // RTC.adjust(DateTime(__DATE__, __TIME__)); // Establece la fecha y hora (Comentar una vez establecida la hora)
}
void loop(){
  DateTime now = RTC.now(); // Obtiene la fecha y hora del RTC
  Serial.print(now.year(), DEC); // A§o
  Serial.print('/');
  Serial.print(now.month(), DEC); // Mes
  Serial.print('/');
  Serial.print(now.day(), DEC); // Dia
  Serial.print(' ');
  Serial.print(now.hour(), DEC); // Horas
  Serial.print(':');
  Serial.print(now.minute(), DEC); // Minutos
  Serial.print(':');
  Serial.print(now.second(), DEC); // Segundos
  Serial.println();
}
